// Logisim project CRC校验(P0.Q1).circ as structural Verilog: 3 circuits, main circuit CRC
module CRC (
  input  [7:0] in_1,
  input  [3:0] in_2,
  output [10:0] out_3
);

  mod mod_1 (
    ._0(1'b0), ._1(1'b0), ._2(1'b0), ._3(in_1[0]), ._4(in_1[1]), ._5(in_1[2]), ._6(in_1[3]), ._7(in_1[4]),
    ._8(in_1[5]), ._9(in_1[6]), ._10(in_1[7]), .in_12(in_2), .out_13(out_3[2:0]));

  assign out_3[10:3] = in_1;
endmodule

module four_bit_motify (
  input  [3:0] in_1,
  input  [3:0] in_2,
  output [2:0] out_3
);

  wire and_1_out, and_2_out, and_3_out, and_4_out;

  and and_1 (and_1_out, in_1[3], in_2[3]);
  and and_2 (and_2_out, and_1_out, in_2[0]);
  and and_3 (and_3_out, in_2[1], and_1_out);
  and and_4 (and_4_out, in_2[2], and_1_out);
  xor xor_1 (out_3[0], in_1[0], and_2_out);
  xor xor_2 (out_3[1], in_1[1], and_3_out);
  xor xor_3 (out_3[2], and_4_out, in_1[2]);
endmodule

module mod (
  input  _0,
  input  _1,
  input  _2,
  input  _3,
  input  _4,
  input  _5,
  input  _6,
  input  _7,
  input  _8,
  input  _9,
  input  _10,
  input  [3:0] in_12,
  output [2:0] out_13
);

  wire [2:0] _1_t, _3_t, _4_t, _5_t, _6_t, four_bit_motify_6_out_3, four_bit_motify_7_out_3;

  four_bit_motify four_bit_motify_1 (.in_1({_6_t, _0}), .in_2(in_12), .out_3(out_13));
  four_bit_motify four_bit_motify_2 (.in_1({_5_t, _1}), .in_2(in_12), .out_3(_6_t));
  four_bit_motify four_bit_motify_3 (.in_1({_4_t, _2}), .in_2(in_12), .out_3(_5_t));
  four_bit_motify four_bit_motify_4 (.in_1({_3_t, _3}), .in_2(in_12), .out_3(_4_t));
  four_bit_motify four_bit_motify_5 (.in_1({_1_t, _4}), .in_2(in_12), .out_3(_3_t));
  four_bit_motify four_bit_motify_6 (.in_1({_10, _9, _8, _7}), .in_2(in_12), .out_3(four_bit_motify_6_out_3));
  four_bit_motify four_bit_motify_7 (
    .in_1({four_bit_motify_6_out_3, _6}), .in_2(in_12), .out_3(four_bit_motify_7_out_3));
  four_bit_motify four_bit_motify_8 (.in_1({four_bit_motify_7_out_3, _5}), .in_2(in_12), .out_3(_1_t));

  // Other names for the same wires on the sheet: _2_t[3:0] = in_12
endmodule
