// Logisim project fsm.circ as structural Verilog: 2 circuits, main circuit fsm
module fsm (
  input  CLR,
  input  [1:0] In,
  output Z
);

  wire clk, comparator_1_eq, comparator_2_eq, comparator_3_eq, or_1_out;
  wire [1:0] multiplexer_1_out, s, s1;

  Clock clock_1 (.out(clk));
  Multiplexer #(.width(2), .enable("false")) multiplexer_1 (.in0(s1), .in1(2'b00), .out(multiplexer_1_out), .sel(CLR));
  Register #(.width(2)) register_1 (.D(multiplexer_1_out), .Q(s), .clk(clk));  // open: en, clr
  transfer transfer_1 (.s01(s[1]), .s00(s[0]), .in1(In[1]), .in0(In[0]), .s11(s1[1]), .s10(s1[0]));
  Comparator #(.width(2)) comparator_1 (.a(In), .b(2'b10), .eq(comparator_1_eq));  // open: gt, lt
  or or_1 (or_1_out, comparator_1_eq, comparator_2_eq);
  Comparator #(.width(2)) comparator_2 (.a(In), .b(2'b00), .eq(comparator_2_eq));  // open: gt, lt
  // Probe on s
  Comparator #(.width(2)) comparator_3 (.a(s), .b(2'b10), .eq(comparator_3_eq));  // open: gt, lt
  and and_1 (Z, or_1_out, comparator_3_eq);

  // Other names for the same wires on the sheet: re = CLR

  // Notes on the sheet:
  //   state storage and clear
  //   next state logic
  //   output logic
endmodule

module transfer (
  input  s01,
  input  s00,
  input  in1,
  input  in0,
  output s11,
  output s10
);

  wire and_1_out, and_2_out, and_3_out, and_4_out, and_5_out, not_1_out, not_2_out, not_3_out, not_4_out,
       not_5_out, not_6_out, not_7_out, not_8_out, not_9_out;

  not not_1 (not_1_out, s01);
  and and_1 (and_1_out, not_1_out, s00, not_2_out);
  not not_2 (not_2_out, in0);
  not not_3 (not_3_out, s00);
  and and_2 (and_2_out, s01, not_3_out, not_4_out);
  not not_4 (not_4_out, in0);
  not not_5 (not_5_out, s01);
  and and_3 (and_3_out, not_5_out, not_6_out, in0);
  not not_6 (not_6_out, in1);
  not not_7 (not_7_out, in1);
  and and_4 (and_4_out, s00, not_7_out, in0);
  not not_8 (not_8_out, s00);
  and and_5 (and_5_out, s01, not_8_out, not_9_out);
  not not_9 (not_9_out, in0);
  or or_1 (s11, and_1_out, and_2_out);
  or or_2 (s10, and_3_out, and_4_out, and_5_out);
endmodule
