// Logisim project ftoi.circ as structural Verilog: 4 circuits, main circuit ftoi
module ftoi (
  input  [15:0] float,
  output [31:0] \int 
);

  wire [1:0] lei_1_out_2;
  wire [31:0] denormal, normal;

  normal normal_1 (.E(float[14:10]), .S(float[15]), .M(float[9:0]), .out_5(normal));  // open: in_4, out_6
  denormal denormal_1 (.E(float[14:10]), .M(float[9:0]), .S(float[15]), .out_4(denormal));
  lei lei_1 (.e(float[14:10]), .out_2(lei_1_out_2));
  // Probe on normal
  // Probe on denormal
  Multiplexer #(.select(2), .width(32), .disabled(0), .enable("false")) multiplexer_1 (
    .in0(normal), .in1(denormal), .in2({32{1'b0}}), .out(\int ), .sel(lei_1_out_2));  // open: in3

  // Other names for the same wires on the sheet: m[9:0] = float[9:0]; e[4:0] = float[14:10]; s = float[15]
endmodule

module lei (
  input  [4:0] e,
  output [1:0] out_2
);

  wire e0, e31, not_1_out, not_2_out;
  wire [0:0] and_1_out;

  Comparator #(.width(5)) comparator_1 (.a(e), .b({5{1'b0}}), .eq(e0));  // open: gt, lt
  Comparator #(.width(5)) comparator_2 (.a(e), .b({5{1'b1}}), .eq(e31));  // open: gt, lt
  not not_1 (not_1_out, e0);
  and and_1 (and_1_out[0], not_1_out, not_2_out);
  not not_2 (not_2_out, e31);
  Multiplexer #(.select(3), .width(2), .disabled(0)) multiplexer_1 (
    .in1(2'b00), .in2(2'b01), .in4(2'b10), .out(out_2), .sel({e31, e0, and_1_out[0]}));  // open: in0, in3, in5, in6, in7, en
endmodule

module normal (
  input  [4:0] E,
  input  S,
  input  [9:0] M,
  input  [31:0] in_4,
  output [31:0] out_5,
  output [31:0] out_6
);

  wire comparator_1_eq, comparator_1_lt;
  wire [4:0] subtractor_1_out;
  wire [31:0] bit_extender_1_out, multiplexer_1_out, multiplexer_2_out, negator_1_out, shifter_1_out,
       shifter_2_out;

  Subtractor #(.width(5)) subtractor_1 (.a(E), .b(5'b01111), .out(subtractor_1_out));  // open: bin, bout
  Comparator #(.width(5)) comparator_1 (
    .a(subtractor_1_out), .b({5{1'b0}}), .eq(comparator_1_eq), .lt(comparator_1_lt));  // open: gt
  assign bit_extender_1_out = {{21{1'b0}}, {1'b1, M}};  // Bit_Extender bit_extender_1
  Multiplexer #(.width(32), .disabled(0), .enable("false")) multiplexer_1 (
    .in0(shifter_2_out), .in1(32'h1), .out(multiplexer_1_out), .sel(comparator_1_eq));
  Multiplexer #(.width(32), .disabled(0), .enable("false")) multiplexer_2 (
    .in0(multiplexer_1_out), .in1({32{1'b0}}), .out(multiplexer_2_out), .sel(comparator_1_lt));
  Shifter #(.width(32)) shifter_1 (.in(bit_extender_1_out), .\dist (subtractor_1_out), .out(shifter_1_out));
  Shifter #(.width(32), .shift("lr")) shifter_2 (.in(shifter_1_out), .\dist (5'b01010), .out(shifter_2_out));
  Multiplexer #(.width(32), .disabled(0), .enable("false")) multiplexer_3 (
    .in0(multiplexer_2_out), .in1(negator_1_out), .out(out_5), .sel(S));
  Negator #(.width(32)) negator_1 (.in(multiplexer_2_out), .out(negator_1_out));
  Negator #(.width(32)) negator_2 (.in(in_4), .out(out_6));
endmodule

module denormal (
  input  [4:0] E,
  input  [9:0] M,
  input  S,
  output [31:0] out_4
);

  wire comparator_1_gt;
  wire [4:0] subtractor_1_out;
  wire [31:0] bit_extender_1_out, multiplexer_1_out, negator_1_out, shifter_1_out, shifter_2_out;

  Subtractor #(.width(5)) subtractor_1 (.a(E), .b(5'b01111), .out(subtractor_1_out));  // open: bin, bout
  Comparator #(.width(5)) comparator_1 (.a(subtractor_1_out), .b({5{1'b0}}), .gt(comparator_1_gt));  // open: eq, lt
  assign bit_extender_1_out = {{22{1'b0}}, M};  // Bit_Extender bit_extender_1
  Multiplexer #(.width(32), .disabled(0)) multiplexer_1 (
    .in0({32{1'b0}}), .in1(shifter_2_out), .out(multiplexer_1_out), .sel(comparator_1_gt));  // open: en
  Shifter #(.width(32)) shifter_1 (.in(bit_extender_1_out), .\dist (subtractor_1_out), .out(shifter_1_out));
  Shifter #(.width(32), .shift("lr")) shifter_2 (.in(shifter_1_out), .\dist (5'b01010), .out(shifter_2_out));
  Negator #(.width(32)) negator_1 (.in(multiplexer_1_out), .out(negator_1_out));
  Multiplexer #(.width(32), .disabled(0)) multiplexer_2 (
    .in0(multiplexer_1_out), .in1(negator_1_out), .out(out_4), .sel(S));  // open: en
endmodule
