// Logisim project logisim导航(P0.Q3).circ as structural Verilog: 1 circuit, main circuit navigation
module navigation (
  input  [1:0] dir,
  input  clk,
  input  reset,
  output arrive,
  output hit
);

  wire and_2_out, and_3_out, and_4_out, and_5_out, comparator_1_eq, comparator_2_eq, comparator_3_eq,
       comparator_4_eq, comparator_5_eq, comparator_6_eq, comparator_7_eq, comparator_8_eq, comparator_9_eq,
       comparator_10_eq, comparator_11_eq, comparator_12_eq, comparator_13_eq, comparator_14_eq,
       comparator_15_eq, decoder_1_out0, decoder_1_out1, decoder_1_out2, decoder_1_out3, not_1_out,
       not_2_out, not_3_out, not_4_out, not_5_out, not_6_out, or_1_out, or_2_out, or_3_out, or_4_out;
  wire [3:0] _0, _1, _2, _3, _4, s, s0, s_prime;

  Register #(.width(4)) y (.D(s_prime), .en(1'b1), .Q(s), .clk(clk), .clr(reset));
  Multiplexer #(.select(4), .width(4), .disabled(0), .enable("false")) multiplexer_1 (
    .in0(_0), .in1(_1), .in2(_2), .in3(_3), .in4(_4), .out(s_prime), .sel(s));  // open: in5, in6, in7, in8, in9, in10, in11, in12, in13, in14, in15
  Register #(.width(4)) register_1 (.D(s), .en(1'b1), .Q(s0), .clk(clk), .clr(reset));
  Multiplexer #(.select(2), .width(4), .disabled(0), .enable("false")) multiplexer_2 (
    .in0(4'b0011), .in1(4'b0100), .in2(4'b0001), .in3(4'b0011), .out(_3), .sel(dir));
  Multiplexer #(.select(2), .width(4), .disabled(0), .enable("false")) multiplexer_3 (
    .in0(4'b0011), .in1(4'b0010), .in2(4'b0000), .in3(4'b0001), .out(_1), .sel(dir));
  Multiplexer #(.select(2), .width(4), .disabled(0), .enable("false")) multiplexer_4 (
    .in0(4'b0001), .in1(4'b0000), .in2(4'b0000), .in3(4'b0000), .out(_0), .sel(dir));
  Comparator #(.width(4)) comparator_1 (.a(s), .b(4'b0100), .eq(comparator_1_eq));  // open: gt, lt
  Comparator #(.width(4)) comparator_2 (.a(s0), .b(4'b0100), .eq(comparator_2_eq));  // open: gt, lt
  Multiplexer #(.select(2), .width(4), .disabled(0), .enable("false")) multiplexer_5 (
    .in0(4'b0000), .in1(4'b0000), .in2(4'b0000), .in3(4'b0000), .out(_4), .sel(dir));
  Multiplexer #(.select(2), .width(4), .disabled(0), .enable("false")) multiplexer_6 (
    .in0(4'b0100), .in1(4'b0010), .in2(4'b0010), .in3(4'b0001), .out(_2), .sel(dir));
  Decoder #(.select(4), .enable("false")) decoder_1 (
    .out0(decoder_1_out0), .out1(decoder_1_out1), .out2(decoder_1_out2), .out3(decoder_1_out3), .sel(s_prime));  // open: out4, out5, out6, out7, out8, out9, out10, out11, out12, out13, out14, out15
  not not_1 (not_1_out, reset);
  and and_1 (arrive, not_1_out, or_1_out);
  or or_1 (or_1_out, comparator_1_eq, comparator_2_eq);
  Comparator #(.width(4)) comparator_3 (.a(s0), .b(4'b0100), .eq(comparator_3_eq));  // open: gt, lt
  not not_2 (not_2_out, comparator_3_eq);
  not not_3 (not_3_out, comparator_4_eq);
  Comparator #(.width(4)) comparator_4 (.a(s0), .b(4'b0001), .eq(comparator_4_eq));  // open: gt, lt
  Comparator #(.width(2)) comparator_5 (.a(dir), .b(2'b01), .eq(comparator_5_eq));  // open: gt, lt
  Comparator #(.width(2)) comparator_6 (.a(dir), .b(2'b10), .eq(comparator_6_eq));  // open: gt, lt
  Comparator #(.width(2)) comparator_7 (.a(dir), .b(2'b11), .eq(comparator_7_eq));  // open: gt, lt
  Comparator #(.width(2)) comparator_8 (.a(dir), .b(2'b11), .eq(comparator_8_eq));  // open: gt, lt
  or or_2 (or_2_out, comparator_5_eq, comparator_6_eq, comparator_7_eq);
  and and_2 (and_2_out, comparator_8_eq, not_5_out, decoder_1_out1);
  Comparator #(.width(2)) comparator_9 (.a(dir), .b(2'b01), .eq(comparator_9_eq));  // open: gt, lt
  Comparator #(.width(2)) comparator_10 (.a(dir), .b(2'b10), .eq(comparator_10_eq));  // open: gt, lt
  and and_3 (and_3_out, or_2_out, not_2_out, not_3_out, decoder_1_out0);
  Comparator #(.width(4)) comparator_11 (.a(s0), .b(4'b0001), .eq(comparator_11_eq));  // open: gt, lt
  or or_3 (or_3_out, comparator_9_eq, comparator_10_eq);
  Comparator #(.width(2)) comparator_12 (.a(dir), .b(2'b11), .eq(comparator_12_eq));  // open: gt, lt
  or or_4 (or_4_out, comparator_12_eq, comparator_13_eq);
  Comparator #(.width(2)) comparator_13 (.a(dir), .b(2'b00), .eq(comparator_13_eq));  // open: gt, lt
  not not_4 (not_4_out, comparator_14_eq);
  Comparator #(.width(4)) comparator_14 (.a(s0), .b(4'b0001), .eq(comparator_14_eq));  // open: gt, lt
  not not_5 (not_5_out, comparator_15_eq);
  Comparator #(.width(4)) comparator_15 (.a(s0), .b(4'b0010), .eq(comparator_15_eq));  // open: gt, lt
  not not_6 (not_6_out, comparator_11_eq);
  and and_4 (and_4_out, or_3_out, not_6_out, decoder_1_out2);
  and and_5 (and_5_out, or_4_out, not_4_out, decoder_1_out3);
  or or_5 (hit, and_3_out, and_2_out, and_4_out, and_5_out);

  // Other names for the same wires on the sheet: re = reset
endmodule
