// Logisim project navigation.circ as structural Verilog: 1 circuit, main circuit navigation
module navigation (
  input  [1:0] dir,
  input  clk,
  input  reset,
  output arrive,
  output hit
);

  wire comparator_2_eq, comparator_3_eq, comparator_4_eq, comparator_5_eq;
  wire [3:0] _0, _1, _2, _3, _4, _5, _6, _7, _8, s, s_prime;

  Multiplexer #(.select(2), .width(4), .disabled(0), .enable("false")) multiplexer_1 (
    .in0(4'b0100), .in1(4'b0111), .in2(4'b0111), .in3(4'b0001), .out(_7), .sel(dir));
  Multiplexer #(.select(2), .width(4), .disabled(0), .enable("false")) multiplexer_2 (
    .in0(4'b0001), .in1(4'b0101), .in2(4'b0101), .in3(4'b0101), .out(_5), .sel(dir));
  Multiplexer #(.select(2), .width(4), .disabled(0), .enable("false")) multiplexer_3 (
    .in0(4'b1000), .in1(4'b0100), .in2(4'b0001), .in3(4'b1000), .out(_3), .sel(dir));
  Multiplexer #(.select(2), .width(4), .disabled(0), .enable("false")) multiplexer_4 (
    .in0(4'b0011), .in1(4'b0010), .in2(4'b0000), .in3(4'b0110), .out(_1), .sel(dir));
  Multiplexer #(.select(2), .width(4), .disabled(0), .enable("false")) multiplexer_5 (
    .in0(4'b0001), .in1(4'b0101), .in2(4'b0101), .in3(4'b0101), .out(_0), .sel(dir));
  Multiplexer #(.select(2), .width(4), .disabled(0), .enable("false")) multiplexer_6 (
    .in0(4'b1000), .in1(4'b0100), .in2(4'b0001), .in3(4'b1000), .out(_8), .sel(dir));
  Multiplexer #(.select(2), .width(4), .disabled(0), .enable("false")) multiplexer_7 (
    .in0(4'b0011), .in1(4'b0010), .in2(4'b0000), .in3(4'b0110), .out(_6), .sel(dir));
  Multiplexer #(.select(2), .width(4), .disabled(0), .enable("false")) multiplexer_8 (
    .in0(4'b0000), .in1(4'b0000), .in2(4'b0000), .in3(4'b0000), .out(_4), .sel(dir));
  Multiplexer #(.select(2), .width(4), .disabled(0), .enable("false")) multiplexer_9 (
    .in0(4'b0100), .in1(4'b0111), .in2(4'b0111), .in3(4'b0001), .out(_2), .sel(dir));
  Register #(.width(4)) register_1 (.D(s_prime), .Q(s), .clk(clk), .clr(reset));  // open: en
  Multiplexer #(.select(4), .width(4), .disabled(0), .enable("false")) multiplexer_10 (
    .in0(_0), .in1(_1), .in2(_2), .in3(_3), .in4(_4), .in5(_5), .in6(_6), .in7(_7), .in8(_8), .out(s_prime),
    .sel(s));  // open: in9, in10, in11, in12, in13, in14, in15
  Comparator #(.width(4)) comparator_1 (.a(s), .b(4'b0100), .eq(arrive));  // open: gt, lt
  Comparator #(.width(4)) comparator_2 (.a(s), .b(4'b0101), .eq(comparator_2_eq));  // open: gt, lt
  Comparator #(.width(4)) comparator_3 (.a(s), .b(4'b0110), .eq(comparator_3_eq));  // open: gt, lt
  Comparator #(.width(4)) comparator_4 (.a(s), .b(4'b0111), .eq(comparator_4_eq));  // open: gt, lt
  Comparator #(.width(4)) comparator_5 (.a(s), .b(4'b1000), .eq(comparator_5_eq));  // open: gt, lt
  or or_1 (hit, comparator_2_eq, comparator_3_eq, comparator_4_eq, comparator_5_eq);

  // Other names for the same wires on the sheet: re = reset

  // Notes on the sheet:
  //   7
  //   5
  //   3
  //   1
  //   0
  //   8
  //   6
  //   4
  //   2
endmodule
