// Logisim project 实现GRF(P0.Q2).circ as structural Verilog: 1 circuit, main circuit grf
module grf (
  input  clk,
  input  reset,
  input  WE,
  input  [4:0] A1,
  input  [4:0] A2,
  input  [4:0] A3,
  input  [31:0] WD,
  output [31:0] RD1,
  output [31:0] RD2
);

  wire and_1_out, and_2_out, e1, e2, e3, e4, e5, e6, e7, e8, e9, e10, e11, e12, e13, e14, e15, e16, e17, e18,
       e19, e20, e21, e22, e23, e24, e25, e26, e27, e28, e29, e30, e31;
  wire [31:0] _028, i1, i2, i3, i4, i5, i6, i7, i8, i9, i10, i11, i12, i13, i14, i15, i16, i17, i18, i19,
       i20, i21, i22, i23, i24, i25, i26, i27, i28, i29, i30, i31, o0, o1, o2, o3, o4, o5, o6, o7, o8, o9,
       o10, o11, o12, o13, o14, o15, o16, o17, o18, o19, o20, o21, o22, o23, o24, o25, o26, o27, o28, o29,
       o30, o31;

  Register #(.width(32)) register_1 (.D(i1), .en(1'b1), .Q(o1), .clk(e1), .clr(reset));
  Register #(.width(32)) register_2 (.en(1'b1), .Q(o0));  // open: D, clk, clr
  Register #(.width(32)) register_3 (.D(i5), .en(1'b1), .Q(o5), .clk(e5), .clr(reset));
  Register #(.width(32)) register_4 (.D(i4), .en(1'b1), .Q(o4), .clk(e4), .clr(reset));
  Register #(.width(32)) register_5 (.D(i8), .en(1'b1), .Q(o8), .clk(e8), .clr(reset));
  Register #(.width(32)) register_6 (.D(i9), .en(1'b1), .Q(o9), .clk(e9), .clr(reset));
  Register #(.width(32)) register_7 (.D(i12), .en(1'b1), .Q(o12), .clk(e12), .clr(reset));
  Register #(.width(32)) register_8 (.D(i16), .en(1'b1), .Q(o16), .clk(e16), .clr(reset));
  Register #(.width(32)) register_9 (.D(i20), .en(1'b1), .Q(o20), .clk(e20), .clr(reset));
  Register #(.width(32)) register_10 (.D(i24), .en(1'b1), .Q(o24), .clk(e24), .clr(reset));
  Register #(.width(32)) register_11 (.D(i28), .en(1'b1), .Q(_028), .clk(e28), .clr(reset));
  Register #(.width(32)) register_12 (.D(i2), .en(1'b1), .Q(o2), .clk(e2), .clr(reset));
  Register #(.width(32)) register_13 (.D(i6), .en(1'b1), .Q(o6), .clk(e6), .clr(reset));
  Register #(.width(32)) register_14 (.D(i13), .en(1'b1), .Q(o13), .clk(e13), .clr(reset));
  Register #(.width(32)) register_15 (.D(i17), .en(1'b1), .Q(o17), .clk(e17), .clr(reset));
  Register #(.width(32)) register_16 (.D(i21), .en(1'b1), .Q(o21), .clk(e21), .clr(reset));
  Register #(.width(32)) register_17 (.D(i25), .en(1'b1), .Q(o25), .clk(e25), .clr(reset));
  Register #(.width(32)) register_18 (.D(i29), .en(1'b1), .Q(o29), .clk(e29), .clr(reset));
  Register #(.width(32)) register_19 (.D(i3), .en(1'b1), .Q(o3), .clk(e3), .clr(reset));
  Register #(.width(32)) register_20 (.D(i7), .en(1'b1), .Q(o7), .clk(e7), .clr(reset));
  Register #(.width(32)) register_21 (.D(i10), .en(1'b1), .Q(o10), .clk(e10), .clr(reset));
  Register #(.width(32)) register_22 (.D(i14), .en(1'b1), .Q(o14), .clk(e14), .clr(reset));
  Register #(.width(32)) register_23 (.D(i18), .en(1'b1), .Q(o18), .clk(e18), .clr(reset));
  Register #(.width(32)) register_24 (.D(i22), .en(1'b1), .Q(o22), .clk(e22), .clr(reset));
  Register #(.width(32)) register_25 (.D(i26), .en(1'b1), .Q(o26), .clk(e26), .clr(reset));
  Register #(.width(32)) register_26 (.D(i30), .en(1'b1), .Q(o30), .clk(e30), .clr(reset));
  Register #(.width(32)) register_27 (.D(i11), .en(1'b1), .Q(o11), .clk(e11), .clr(reset));
  Register #(.width(32)) register_28 (.D(i15), .en(1'b1), .Q(o15), .clk(e15), .clr(reset));
  Register #(.width(32)) register_29 (.D(i19), .en(1'b1), .Q(o19), .clk(e19), .clr(reset));
  Register #(.width(32)) register_30 (.D(i23), .en(1'b1), .Q(o23), .clk(e23), .clr(reset));
  Register #(.width(32)) register_31 (.D(i27), .en(1'b1), .Q(o27), .clk(e27), .clr(reset));
  Register #(.width(32)) register_32 (.D(i31), .en(1'b1), .Q(o31), .clk(e31), .clr(reset));
  Multiplexer #(.select(5), .width(32)) multiplexer_1 (
    .in0(o0), .in1(o1), .in2(o2), .in3(o3), .in4(o4), .in5(o5), .in6(o6), .in7(o7), .in8(o8), .in9(o9),
    .in10(o10), .in11(o11), .in12(o12), .in13(o13), .in14(o14), .in15(o15), .in16(o16), .in17(o17),
    .in18(o18), .in19(o19), .in20(o20), .in21(o21), .in22(o22), .in23(o23), .in24(o24), .in25(o25),
    .in26(o26), .in27(o27), .in28(o28), .in29(o29), .in30(o30), .in31(o31), .out(RD1), .sel(A1), .en(1'b1));
  and and_1 (and_1_out, WE, clk);
  Decoder #(.select(5), .disabled(0)) decoder_1 (
    .out1(e1), .out2(e2), .out3(e3), .out4(e4), .out5(e5), .out6(e6), .out7(e7), .out8(e8), .out9(e9),
    .out10(e10), .out11(e11), .out12(e12), .out13(e12), .out14(e13), .out15(e14), .out16(e16), .out17(e17),
    .out18(e18), .out19(e19), .out20(e20), .out21(e21), .out22(e22), .out23(e23), .out24(e24), .out25(e25),
    .out26(e26), .out27(e27), .out28(e28), .out29(e29), .out30(e30), .out31(e31), .sel(A3), .en(and_1_out));  // open: out0
  Multiplexer #(.select(5), .width(32)) multiplexer_2 (
    .in0(o0), .in1(o1), .in2(o2), .in3(o3), .in4(o4), .in5(o5), .in6(o6), .in7(o7), .in8(o8), .in9(o9),
    .in10(o10), .in11(o11), .in12(o12), .in13(o13), .in14(o14), .in15(o15), .in16(o16), .in17(o17),
    .in18(o18), .in19(o19), .in20(o20), .in21(o21), .in22(o22), .in23(o23), .in24(o24), .in25(o25),
    .in26(o26), .in27(o27), .in28(o28), .in29(o29), .in30(o30), .in31(o31), .out(RD2), .sel(A2), .en(1'b1));
  Demultiplexer #(.select(5), .width(32), .disabled(0)) demultiplexer_1 (
    .out1(i1), .out2(i2), .out3(i3), .out4(i4), .out5(i5), .out6(i6), .out7(i7), .out8(i8), .out9(i9),
    .out10(i10), .out11(i11), .out12(i12), .out13(i13), .out14(i14), .out15(i15), .out16(i16), .out17(i17),
    .out18(i18), .out19(i19), .out20(i20), .out21(i21), .out22(i22), .out23(i23), .out24(i24), .out25(i25),
    .out26(i26), .out27(i27), .out28(i28), .out29(i29), .out30(i30), .out31(i31), .in(WD), .sel(A3),
    .en(and_2_out));  // open: out0
  and and_2 (and_2_out, WE, clk);

  // Other names for the same wires on the sheet: out1[31:0] = RD1; out2[31:0] = RD2; re = reset; w[31:0] = WD
endmodule
