// Logisim project 状态机.circ as structural Verilog: 5 circuits, main circuit moore
module moore (
  input  \input ,
  input  clr,
  output out_3
);

  wire clk;
  wire [3:0] next_state, s_prime, state_storage_q, state_transfer_1_out_3;

  Clock clock_1 (.out(clk));
  state_transfer state_transfer_1 (.\input (\input ), .state_now(state_storage_q), .out_3(state_transfer_1_out_3));
  Multiplexer #(.width(4)) multiplexer_1 (.in0(next_state), .in1(4'b0000), .out(s_prime), .sel(clr));  // open: en
  Register #(.width(4)) state_storage (.D(state_transfer_1_out_3), .Q(state_storage_q), .clk(clk));  // open: en, clr
  output_moore output_logic (.state_now(state_storage_q), .out(out_3));

  // Other names for the same wires on the sheet: reset = clr

  // Notes on the sheet:
  //   state_transfer
endmodule

module mealy (
  input  \input ,
  output out_2
);

  wire clk;
  wire [3:0] state_storage_q, state_transfer_out_3;

  Clock clock_1 (.out(clk));
  state_transfer state_transfer (.\input (\input ), .state_now(state_storage_q), .out_3(state_transfer_out_3));
  Register #(.width(4)) state_storage (.D(state_transfer_out_3), .Q(state_storage_q), .clk(clk));  // open: en, clr
  output_mealy output_logic (.\input (\input ), .state_now(state_storage_q), .out(out_2));
endmodule

module state_transfer (
  input  \input ,
  input  [3:0] state_now,
  output [3:0] out_3
);


  assign out_3 = 4'b1111;
endmodule

module output_moore (
  input  [3:0] state_now,
  output out
);
endmodule

module output_mealy (
  input  \input ,
  input  [3:0] state_now,
  output out
);
endmodule
