// Logisim project P3.circ as structural Verilog: 11 circuits, main circuit main
module main (
  input  in_1,
  output [31:0] instr,
  output regWrite,
  output [4:0] out_4,
  output [31:0] regData,
  output memWrite,
  output [4:0] memAddr,
  output [31:0] memData
);

  wire aluSrc, branch, clk, extOp, jump, memRead, regDst, zero;
  wire [1:0] memToReg;
  wire [2:0] aluCtrl;
  wire [4:0] spliter_1_rd, spliter_1_rs, spliter_1_rt;
  wire [5:0] spliter_1_funcode, spliter_1_opcode;
  wire [15:0] spliter_1_imm16;
  wire [31:0] ALU_result, DM_rd, EXT_out, GRF_rd1, multiplexer_2_out;

  IFU IFU (.reset(in_1), .clk(clk), .zero(zero), .branch(branch), .imm32(EXT_out), .instr(instr));
  spliter spliter_1 (
    .in_1(instr), .opcode(spliter_1_opcode), .rs(spliter_1_rs), .rt(spliter_1_rt), .rd(spliter_1_rd),
    .funcode(spliter_1_funcode), .imm16(spliter_1_imm16));  // open: add26
  Multiplexer #(.width(5)) multiplexer_1 (
    .in0(spliter_1_rt), .in1(spliter_1_rd), .out(out_4), .sel(regDst));  // open: en
  Ctrl ctrl_unit (
    .op(spliter_1_opcode), .func(spliter_1_funcode), .memToReg(memToReg), .regDst(regDst), .aluSrc(aluSrc),
    .regWrite(regWrite), .memRead(memRead), .memWrite(memWrite), .extOp(extOp), .branch(branch),
    .aluCtrl(aluCtrl), .jump(jump));
  EXT EXT (.extOp(extOp), .in(spliter_1_imm16), .out(EXT_out));
  GRF GRF (
    .ra1(spliter_1_rs), .ra2(spliter_1_rt), .wa(out_4), .wd(regData), .clk(clk), .reset(in_1), .we(regWrite),
    .rd1(GRF_rd1), .rd2(memData));
  Multiplexer #(.width(32)) multiplexer_2 (
    .in0(memData), .in1(EXT_out), .out(multiplexer_2_out), .sel(aluSrc));  // open: en
  ALU ALU (
    .A(GRF_rd1), .B(multiplexer_2_out), .aluCtrl(aluCtrl),
    .result({ALU_result[31:7], memAddr, ALU_result[1:0]}), .zero(zero));
  Clock clock_1 (.out(clk));
  DM DM (
    .a({ALU_result[31:7], memAddr, ALU_result[1:0]}), .wd(memData), .clk(clk), .reset(in_1),
    .memWrite(memWrite), .MemRead(memRead), .rd(DM_rd));
  Multiplexer #(.select(2), .width(32)) multiplexer_3 (
    .in0({ALU_result[31:7], memAddr, ALU_result[1:0]}), .in1({spliter_1_imm16, {16{1'b0}}}), .in2(DM_rd),
    .out(regData), .sel(memToReg));  // open: in3, en

  // Other names for the same wires on the sheet: regAddr[4:0] = out_4; reset = in_1
endmodule

module test (
  input  reset,
  output [31:0] out_2,
  output out_3,
  output [4:0] out_4,
  output [31:0] out_5,
  output out_6,
  output [4:0] out_7,
  output halt,
  output [31:0] out_9
);

  wire clock_1_out, comparator_1_eq, multiplexer_1_out;
  wire [4:0] counter_1_q;

  Clock clock_1 (.out(clock_1_out));
  Counter #(.width(5), .max('h1f), .ongoal("stay")) counter_1 (
    .Q(counter_1_q), .carry(halt), .clk(clock_1_out), .clr(reset));  // open: load, D, count
  Comparator #(.width(5), .mode("unsigned")) comparator_1 (
    .a({5{1'b1}}), .b(counter_1_q), .eq(comparator_1_eq));  // open: gt, lt
  Multiplexer multiplexer_1 (
    .in0(clock_1_out), .in1(1'b0), .out(multiplexer_1_out), .sel(comparator_1_eq));  // open: en
  main main_1 (
    .in_1(reset), .instr(out_2), .regWrite(out_3), .out_4(out_4), .regData(out_5), .memWrite(out_6),
    .memAddr(out_7), .memData(out_9));
endmodule

module Ctrl (
  input  [5:0] op,
  input  [5:0] func,
  output [1:0] memToReg,
  output regDst,
  output aluSrc,
  output regWrite,
  output memRead,
  output memWrite,
  output extOp,
  output branch,
  output [2:0] aluCtrl,
  output jump
);

  wire not_1_out, not_2_out, not_3_out, not_4_out, not_5_out, not_6_out;
  wire [1:0] or_4_out;

  not not_1 (not_1_out, op[5]);
  not not_2 (not_2_out, op[4]);
  not not_3 (not_3_out, op[2]);
  not not_4 (not_4_out, op[3]);
  not not_5 (not_5_out, op[1]);
  not not_6 (not_6_out, op[0]);
  and R (regDst, not_6_out, not_5_out, not_3_out, not_4_out, not_2_out, not_1_out);
  and lw (memRead, op[5], not_2_out, not_4_out, not_3_out, op[1], op[0]);
  and sw (memWrite, op[5], not_2_out, op[3], not_3_out, op[1], op[0]);
  and beq (branch, not_1_out, not_2_out, not_4_out, op[2], not_5_out, not_6_out);
  and lui (memToReg[0], not_1_out, not_2_out, op[3], op[2], op[1], op[0]);
  and ori (extOp, not_1_out, not_2_out, op[3], op[2], not_5_out, op[0]);
  and j (jump, not_1_out, not_2_out, not_4_out, not_3_out, op[1], not_6_out);
  or or_1 (aluSrc, memRead, memWrite, extOp);
  or or_2 (regWrite, regDst, memRead, memToReg[0], extOp);
  or or_3 (or_4_out[1], branch, memToReg[0], extOp);
  or or_4 (or_4_out[0], memRead, memWrite, memToReg[0], extOp);
  AluCtrl aluctrl_1 (.aluOp({extOp, or_4_out}), .func(func), .out_3(aluCtrl));

  assign memToReg[1] = memRead;
endmodule

module AluCtrl (
  input  [2:0] aluOp,
  input  [5:0] func,
  output [2:0] out_3
);

  wire addu_out, beq_out, not_1_out, not_2_out, not_3_out, not_4_out, not_5_out, not_6_out, not_7_out,
       not_8_out, not_9_out, ori_out, subu_out, sw_lw_out;

  not not_1 (not_1_out, aluOp[2]);
  not not_2 (not_2_out, aluOp[1]);
  not not_3 (not_3_out, aluOp[0]);
  not not_4 (not_4_out, func[5]);
  not not_5 (not_5_out, func[3]);
  not not_6 (not_6_out, func[4]);
  not not_7 (not_7_out, func[1]);
  not not_8 (not_8_out, func[2]);
  not not_9 (not_9_out, func[0]);
  and sw_lw (sw_lw_out, not_1_out, not_2_out, aluOp[0]);
  and beq (beq_out, not_1_out, aluOp[1], not_3_out);
  and lui_j (out_3[2], not_1_out, aluOp[1], aluOp[0]);
  and ori (ori_out, aluOp[2], aluOp[1], aluOp[0]);
  and addu (addu_out, not_1_out, not_2_out, not_3_out, func[5], not_6_out, not_5_out, not_8_out, not_7_out, func[0]);
  and subu (subu_out, not_1_out, not_2_out, not_3_out, func[5], not_6_out, not_5_out, not_8_out, func[1], func[0]);
  or or_1 (out_3[1], sw_lw_out, beq_out, out_3[2], addu_out, subu_out);
  or or_2 (out_3[0], beq_out, out_3[2], subu_out, ori_out);
endmodule

module ALU (
  input  [31:0] A,
  input  [31:0] B,
  input  [2:0] aluCtrl,
  output [31:0] result,
  output zero
);

  wire comparator_1_gt;
  wire [31:0] adder_1_out, and_1_out, bit_extender_1_out, or_1_out, subtractor_1_out;

  assign and_1_out = A & B;  // AND_Gate and_1, 32 bits wide
  assign or_1_out = A | B;  // OR_Gate or_1, 32 bits wide
  Adder #(.width(32)) adder_1 (.a(A), .b(B), .out(adder_1_out));  // open: cin, cout
  Subtractor #(.width(32)) subtractor_1 (.a(A), .b(B), .out(subtractor_1_out));  // open: bin, bout
  assign bit_extender_1_out = {{31{1'b0}}, comparator_1_gt};  // Bit_Extender bit_extender_1
  Comparator #(.width(32)) comparator_1 (.a(A), .b(B), .gt(comparator_1_gt), .eq(zero));  // open: lt
  Multiplexer #(.select(3), .width(32)) multiplexer_1 (
    .in0(and_1_out), .in1(or_1_out), .in2(adder_1_out), .in3(subtractor_1_out), .in5(bit_extender_1_out),
    .out(result), .sel(aluCtrl));  // open: in4, in6, in7, en
endmodule

module IFU (
  input  reset,
  input  clk,
  input  zero,
  input  branch,
  input  [31:0] imm32,
  output [31:0] instr
);

  wire and_1_out, comparator_1_eq;
  wire [31:0] adder_1_out, adder_2_out, multiplexer_1_out, npc, pc, register_1_q, register_2_q, shifter_1_out;

  Shifter #(.width(32)) shifter_1 (.in(imm32), .\dist (5'b00010), .out(shifter_1_out));
  Adder #(.width(32)) adder_1 (.a(register_1_q), .b(32'h4), .out(adder_1_out));  // open: cin, cout
  and and_1 (and_1_out, zero, branch);
  Adder #(.width(32)) adder_2 (.a(adder_1_out), .b(shifter_1_out), .out(adder_2_out));  // open: cin, cout
  Multiplexer #(.width(32)) multiplexer_1 (
    .in0(adder_1_out), .in1(adder_2_out), .out(multiplexer_1_out), .sel(and_1_out));  // open: en
  Register #(.width(32)) register_1 (.D(multiplexer_1_out), .Q(register_1_q), .clk(clk), .clr(reset));  // open: en
  Register #(.width(32)) register_2 (.D(npc), .Q(register_2_q), .clk(clk), .clr(reset));  // open: en
  Comparator #(.width(32), .mode("unsigned")) comparator_1 (
    .a({32{1'b0}}), .b(register_2_q), .eq(comparator_1_eq));  // open: gt, lt
  IM IM (.addr(register_1_q[6:2]), .instr(instr));
  Multiplexer #(.width(32)) multiplexer_2 (.in0(register_2_q), .out(pc), .sel(comparator_1_eq));  // open: in1, en
  Multiplexer #(.width(32)) multiplexer_3 (.in0(npc), .in1(32'h3000), .out(pc), .sel(reset));  // open: en

  // Other names for the same wires on the sheet: imm[31:0] = imm32; re = reset

  // Notes on the sheet:
  //   异步复位至0x00003000
  //   同步复位
endmodule

module EXT (
  input  extOp,
  input  [15:0] in,
  output [31:0] out
);

  wire [31:0] bit_extender_1_out, bit_extender_2_out;

  assign bit_extender_1_out = {{16{in[15]}}, in};  // Bit_Extender bit_extender_1
  assign bit_extender_2_out = {{16{1'b0}}, in};  // Bit_Extender bit_extender_2
  Multiplexer #(.width(32)) multiplexer_1 (
    .in0(bit_extender_1_out), .in1(bit_extender_2_out), .out(out), .sel(extOp));  // open: en
endmodule

module GRF (
  input  clk,
  input  reset,
  input  we,
  input  [4:0] ra1,
  input  [4:0] ra2,
  input  [4:0] wa,
  input  [31:0] wd,
  output [31:0] rd1,
  output [31:0] rd2
);

  wire [31:0] i1, i2, i3, i4, i5, i6, i7, i8, i9, i10, i11, i12, i13, i14, i15, i16, i17, i18, i19, i20, i21,
       i22, i23, i24, i25, i26, i27, i28, i29, i30, i31, o0, o1, o2, o3, o4, o5, o6, o7, o8, o9, o10, o11,
       o12, o13, o14, o15, o16, o17, o18, o19, o20, o21, o22, o23, o24, o25, o26, o27, o28, o29, o30, o31;

  Register #(.width(32)) register_1 (.D({32{1'b0}}), .Q(o0), .clk(clk), .clr(reset));  // open: en
  Register #(.width(32)) register_2 (.D(i4), .en(we), .Q(o4), .clk(clk), .clr(reset));
  Register #(.width(32)) register_3 (.D(i8), .en(we), .Q(o8), .clk(clk), .clr(reset));
  Register #(.width(32)) register_4 (.D(i12), .en(we), .Q(o12), .clk(clk), .clr(reset));
  Register #(.width(32)) register_5 (.D(i16), .en(we), .Q(o16), .clk(clk), .clr(reset));
  Register #(.width(32)) register_6 (.D(i20), .en(we), .Q(o20), .clk(clk), .clr(reset));
  Register #(.width(32)) register_7 (.D(i24), .en(we), .Q(o24), .clk(clk), .clr(reset));
  Register #(.width(32)) register_8 (.D(i28), .en(we), .Q(o28), .clk(clk), .clr(reset));
  Register #(.width(32)) register_9 (.D(i1), .en(we), .Q(o1), .clk(clk), .clr(reset));
  Register #(.width(32)) register_10 (.D(i5), .en(we), .Q(o5), .clk(clk), .clr(reset));
  Register #(.width(32)) register_11 (.D(i9), .en(we), .Q(o9), .clk(clk), .clr(reset));
  Register #(.width(32)) register_12 (.D(i13), .en(we), .Q(o13), .clk(clk), .clr(reset));
  Register #(.width(32)) register_13 (.D(i17), .en(we), .Q(o17), .clk(clk), .clr(reset));
  Register #(.width(32)) register_14 (.D(i21), .en(we), .Q(o21), .clk(clk), .clr(reset));
  Register #(.width(32)) register_15 (.D(i25), .en(we), .Q(o25), .clk(clk), .clr(reset));
  Register #(.width(32)) register_16 (.D(i29), .en(we), .Q(o29), .clk(clk), .clr(reset));
  Register #(.width(32)) register_17 (.D(i2), .en(we), .Q(o2), .clk(clk), .clr(reset));
  Register #(.width(32)) register_18 (.D(i6), .en(we), .Q(o6), .clk(clk), .clr(reset));
  Register #(.width(32)) register_19 (.D(i10), .en(we), .Q(o10), .clk(clk), .clr(reset));
  Register #(.width(32)) register_20 (.D(i3), .en(we), .Q(o3), .clk(clk), .clr(reset));
  Register #(.width(32)) register_21 (.D(i7), .en(we), .Q(o7), .clk(clk), .clr(reset));
  Register #(.width(32)) register_22 (.D(i14), .en(we), .Q(o14), .clk(clk), .clr(reset));
  Register #(.width(32)) register_23 (.D(i18), .en(we), .Q(o18), .clk(clk), .clr(reset));
  Register #(.width(32)) register_24 (.D(i22), .en(we), .Q(o22), .clk(clk), .clr(reset));
  Register #(.width(32)) register_25 (.D(i26), .en(we), .Q(o26), .clk(clk), .clr(reset));
  Register #(.width(32)) register_26 (.D(i30), .en(we), .Q(o30), .clk(clk), .clr(reset));
  Register #(.width(32)) register_27 (.D(i11), .en(we), .Q(o11), .clk(clk), .clr(reset));
  Register #(.width(32)) register_28 (.D(i15), .en(we), .Q(o15), .clk(clk), .clr(reset));
  Register #(.width(32)) register_29 (.D(i19), .en(we), .Q(o19), .clk(clk), .clr(reset));
  Register #(.width(32)) register_30 (.D(i23), .en(we), .Q(o23), .clk(clk), .clr(reset));
  Register #(.width(32)) register_31 (.D(i27), .en(we), .Q(o27), .clk(clk), .clr(reset));
  Register #(.width(32)) register_32 (.D(i31), .en(we), .Q(o31), .clk(clk), .clr(reset));
  Multiplexer #(.select(5), .width(32), .disabled(0), .enable("false")) multiplexer_1 (
    .in0(o0), .in1(o1), .in2(o2), .in3(o3), .in4(o4), .in5(o5), .in6(o6), .in7(o7), .in8(o8), .in9(o9),
    .in10(o10), .in11(o11), .in12(o12), .in13(o13), .in14(o14), .in15(o15), .in16(o16), .in17(o17),
    .in18(o18), .in19(o19), .in20(o20), .in21(o21), .in22(o22), .in23(o23), .in24(o24), .in25(o25),
    .in26(o26), .in27(o27), .in28(o28), .in29(o29), .in30(o30), .in31(o31), .out(rd1), .sel(ra1));
  Multiplexer #(.select(5), .width(32), .disabled(0), .enable("false")) multiplexer_2 (
    .in0(o0), .in1(o1), .in2(o2), .in3(o3), .in4(o4), .in5(o5), .in6(o6), .in7(o7), .in8(o8), .in9(o9),
    .in10(o10), .in11(o11), .in12(o12), .in13(o13), .in14(o14), .in15(o15), .in16(o16), .in17(o17),
    .in18(o18), .in19(o19), .in20(o20), .in21(o21), .in22(o22), .in23(o23), .in24(o24), .in25(o25),
    .in26(o26), .in27(o27), .in28(o28), .in29(o29), .in30(o30), .in31(o31), .out(rd2), .sel(ra2));
  Demultiplexer #(.select(5), .width(32), .tristate("true")) demultiplexer_1 (
    .out1(i1), .out2(i2), .out3(i3), .out4(i4), .out5(i5), .out6(i6), .out7(i7), .out8(i8), .out9(i9),
    .out10(i10), .out11(i11), .out12(i12), .out13(i13), .out14(i14), .out15(i15), .out16(i16), .out17(i17),
    .out18(i18), .out19(i19), .out20(i20), .out21(i21), .out22(i22), .out23(i23), .out24(i24), .out25(i25),
    .out26(i26), .out27(i27), .out28(i28), .out29(i29), .out30(i30), .out31(i31), .in(wd), .sel(wa));  // open: out0, en

  // Other names for the same wires on the sheet: a1[4:0] = ra1; a2[4:0] = ra2; a3[4:0] = wa; e1 = we; e2 = we;
  //   e3 = we; e4 = we; e5 = we; e6 = we; e7 = we; e8 = we; e9 = we; e10 = we; e11 = we; e12 = we; e13 = we; e14 = we;
  //   e15 = we; e16 = we; e17 = we; e18 = we; e19 = we; e20 = we; e21 = we; e22 = we; e23 = we; e24 = we; e25 = we;
  //   e26 = we; e27 = we; e28 = we; e29 = we; e30 = we; e31 = we; out1[31:0] = rd1; out2[31:0] = rd2; re = reset;
  //   w[31:0] = wd
endmodule

module DM (
  input  [31:0] a,
  input  [31:0] wd,
  input  clk,
  input  reset,
  input  memWrite,
  input  MemRead,
  output [31:0] rd
);

  RAM #(.addrWidth(5), .dataWidth(32), .bus("separate")) ram_1 (
    .addr(a[6:2]), .din(wd), .data(rd), .str(memWrite), .clk(clk), .ld(MemRead), .clr(reset));  // open: sel
endmodule

module IM (
  input  [4:0] addr,
  output [31:0] instr
);

  ROM #(.addrWidth(5), .dataWidth(32)) rom_1 (.addr(addr), .data(instr));  // open: sel

  // Notes on the sheet:
  //   contents of rom_1 (hex, n*v repeats v):
  //   34100004 34110008 3412000c 8e080000 ae100000 ae320004 8e090000 8e2a0000 8e2bfffc 8e2c0004 8e4d0000
endmodule

module spliter (
  input  [31:0] in_1,
  output [5:0] opcode,
  output [4:0] rs,
  output [4:0] rt,
  output [4:0] rd,
  output [5:0] funcode,
  output [15:0] imm16,
  output [25:0] add26
);

  Bit_Extender #(.in_width(32)) bit_extender_1 (.in(in_1), .out(imm16));
  Bit_Extender #(.in_width(32), .out_width(26)) bit_extender_2 (.in(in_1), .out(add26));

  assign funcode = in_1[5:0];
  assign opcode = in_1[31:26];
  assign rd = in_1[15:11];
  assign rs = in_1[25:21];
  assign rt = in_1[20:16];
endmodule
