// Logisim project 2^n_mod5.circ as structural Verilog: 2 circuits, main circuit mod5
module mod5 (
  input  i1,
  output out_2,
  output out_3,
  output out_4,
  output out_5,
  output out_6
);

  wire clock_1_out, i0_q, not_1_out, not_2_out;

  Register #(.width(1)) i0 (.D(i1), .Q(i0_q), .clk(clock_1_out));  // open: en, clr
  Clock clock_1 (.out(clock_1_out));
  not not_1 (not_1_out, i1);
  not not_2 (not_2_out, i0_q);
  and o1 (out_3, not_1_out, not_2_out);
  and o2 (out_4, not_2_out, i1);
  and o3 (out_5, i0_q, i1);
  and o4 (out_6, i0_q, not_1_out);

  assign out_2 = 1'b0;
endmodule

module test (
  output out_1,
  output out_2,
  output out_3,
  output out_4,
  output out_5,
  output out_6,
  output out_7
);

  wire clock_1_out;
  wire [3:0] counter_1_q;

  Counter #(.width(4), .max('hf)) counter_1 (
    .Q(counter_1_q), .carry(out_7), .clk(clock_1_out));  // open: load, D, count, clr
  Clock clock_1 (.out(clock_1_out));
  mod5 mod5_1 (.i1(out_1), .out_2(out_2), .out_3(out_3), .out_4(out_4), .out_5(out_5), .out_6(out_6));
  ROM #(.addrWidth(4), .dataWidth(1)) rom_1 (.addr(counter_1_q), .data(out_1));  // open: sel

  // Notes on the sheet:
  //   contents of rom_1 (hex, n*v repeats v):
  //   0 1 0 0 1 0 0 1 0 0 1 0 0 1
endmodule
