// Logisim project febnacci.circ as structural Verilog: 2 circuits, main circuit test
module test (
  input  [2:0] in_1,
  output [3:0] out_2
);

  wire clock_1_out, counter_1_carry;
  wire [3:0] main_1_out_2;

  Clock clock_1 (.out(clock_1_out));
  Counter #(.width(6), .max('h3f)) counter_1 (
    .carry(counter_1_carry), .clk(clock_1_out));  // open: load, D, count, Q, clr
  main main_1 (.in_1(in_1), .out_2(main_1_out_2));
  Register #(.width(4)) register_1 (.D(main_1_out_2), .Q(out_2), .clk(counter_1_carry));  // open: en, clr
endmodule

module main (
  input  [2:0] in_1,
  output [3:0] out_2
);

  wire clock_1_out, comparator_1_gt, comparator_2_eq, comparator_2_lt, or_1_out;
  wire [2:0] counter_1_q;
  wire [3:0] adder_1_out, multiplexer_1_out, register_2_q;

  Counter #(.width(3), .max('h7)) counter_1 (.Q(counter_1_q), .clk(or_1_out));  // open: load, D, count, carry, clr
  Clock clock_1 (.out(clock_1_out));
  Comparator #(.width(3)) comparator_1 (.a(counter_1_q), .b(3'b000), .gt(comparator_1_gt));  // open: eq, lt
  Comparator #(.width(3)) comparator_2 (
    .a(in_1), .b(counter_1_q), .eq(comparator_2_eq), .lt(comparator_2_lt));  // open: gt
  or or_1 (or_1_out, comparator_2_eq, comparator_2_lt, clock_1_out);
  Multiplexer #(.width(4)) multiplexer_1 (
    .in0(4'b0001), .in1(adder_1_out), .out(multiplexer_1_out), .sel(comparator_1_gt));  // open: en
  Register #(.width(4)) register_1 (.D(multiplexer_1_out), .Q(out_2), .clk(or_1_out));  // open: en, clr
  Register #(.width(4)) register_2 (.D(out_2), .Q(register_2_q), .clk(or_1_out));  // open: en, clr
  Adder #(.width(4)) adder_1 (.a(out_2), .b(register_2_q), .out(adder_1_out));  // open: cin, cout
endmodule
