// Logisim project febonacci_fast.circ as structural Verilog: 8 circuits, main circuit main
module main (
  input  [31:0] in_1,
  input  in_2,
  output [31:0] out_3
);

  wire cnt_1_freeze, cnt_1_n_low;

  cnt cnt_1 (.in_1(in_1), .re(in_2), .n_low(cnt_1_n_low), .freeze(cnt_1_freeze));
  calculate calculate_1 (.n_low(cnt_1_n_low), .freeze(cnt_1_freeze), .re(in_2), .out_4(out_3));

  // Other names for the same wires on the sheet: input[31:0] = in_1; output[31:0] = out_3
endmodule

module cnt (
  input  [31:0] in_1,
  input  re,
  output n_low,
  output freeze
);

  wire \begin , clk, comparator_1_eq;
  wire [31:0] multiplexer_1_out, n, shifter_1_out;

  Counter #(.width(1), .max('h1), .ongoal("stay")) counter_1 (
    .Q(\begin ), .clk(clk), .clr(re));  // open: load, D, count, carry
  Clock u_clk (.out(clk));
  Shifter #(.width(32), .shift("lr")) shifter_1 (.in(n), .\dist (5'b00001), .out(shifter_1_out));
  Bit_Extender #(.in_width(32), .out_width(1)) bit_extender_1 (.in(n), .out(n_low));
  Comparator #(.width(32), .mode("unsigned")) comparator_1 (
    .a(n), .b({32{1'b0}}), .eq(comparator_1_eq));  // open: gt, lt
  Multiplexer #(.width(32), .disabled(0)) multiplexer_1 (
    .in0(in_1), .in1(shifter_1_out), .out(multiplexer_1_out), .sel(\begin ));  // open: en
  Multiplexer multiplexer_2 (.in0(1'b0), .in1(comparator_1_eq), .out(freeze), .sel(\begin ));  // open: en
  Register #(.width(32)) register_1 (.D(multiplexer_1_out), .Q(n), .clk(clk), .clr(re));  // open: en
endmodule

module calculate (
  input  n_low,
  input  freeze,
  input  re,
  output [31:0] out_4
);

  wire \begin , clk, en;
  wire [31:0] a00, a01, a10, a11, matrix_begin_1_a00, matrix_begin_1_a01, matrix_begin_1_a10,
       matrix_begin_1_a11, matrix_multi_1_c00, matrix_multi_1_c01, matrix_multi_1_c10, matrix_multi_1_c11,
       matrix_multi_2_c00, matrix_multi_2_c01, matrix_multi_2_c10, matrix_multi_2_c11, matrix_mux_1_c00,
       matrix_mux_1_c01, matrix_mux_1_c10, matrix_mux_1_c11, matrix_mux_2_c00, matrix_mux_2_c01,
       matrix_mux_2_c10, matrix_mux_2_c11, matrix_mux_3_c00, matrix_mux_3_c01, matrix_mux_3_c10,
       matrix_mux_3_c11, s00, s01, s10, s11, unit_matirx_1_e00, unit_matirx_1_e01, unit_matirx_1_e10,
       unit_matirx_1_e11, unit_matirx_2_e00, unit_matirx_2_e01, unit_matirx_2_e10, unit_matirx_2_e11;

  Counter #(.width(1), .max('h1), .ongoal("stay")) counter_1 (
    .Q(\begin ), .clk(clk), .clr(re));  // open: load, D, count, carry
  Clock u_clk (.out(clk));
  matrix_begin matrix_begin_1 (
    .A00(matrix_begin_1_a00), .A01(matrix_begin_1_a01), .A10(matrix_begin_1_a10), .A11(matrix_begin_1_a11));
  matrix_multi matrix_multi_1 (
    .a00(a00), .a01(a01), .a10(a10), .a11(a11), .b00(a00), .b01(a01), .b10(a10), .b11(a11),
    .c00(matrix_multi_1_c00), .c01(matrix_multi_1_c01), .c10(matrix_multi_1_c10), .c11(matrix_multi_1_c11));
  unit_matirx unit_matirx_1 (
    .E00(unit_matirx_1_e00), .E01(unit_matirx_1_e01), .E10(unit_matirx_1_e10), .E11(unit_matirx_1_e11));
  matrix_mux matrix_mux_1 (
    .a00(matrix_begin_1_a00), .a01(matrix_begin_1_a01), .a10(matrix_begin_1_a10), .a11(matrix_begin_1_a11),
    .b00(matrix_multi_1_c00), .b01(matrix_multi_1_c01), .b10(matrix_multi_1_c10), .b11(matrix_multi_1_c11),
    .sel(\begin ), .c00(matrix_mux_1_c00), .c01(matrix_mux_1_c01), .c10(matrix_mux_1_c10),
    .c11(matrix_mux_1_c11));
  matrix_mux matrix_mux_2 (
    .a00(unit_matirx_1_e00), .a01(unit_matirx_1_e01), .a10(unit_matirx_1_e10), .a11(unit_matirx_1_e11),
    .b00(a00), .b01(a01), .b10(a10), .b11(a11), .sel(n_low), .c00(matrix_mux_2_c00), .c01(matrix_mux_2_c01),
    .c10(matrix_mux_2_c10), .c11(matrix_mux_2_c11));
  grf A_matrix (
    .a00_in(matrix_mux_1_c00), .a01_in(matrix_mux_1_c01), .a10_in(matrix_mux_1_c10),
    .a11_in(matrix_mux_1_c11), .en(en), .clk(clk), .re(re), .a00_out(a00), .a01_out(a01), .a10_out(a10),
    .a11_out(a11));
  unit_matirx unit_matirx_2 (
    .E00(unit_matirx_2_e00), .E01(unit_matirx_2_e01), .E10(unit_matirx_2_e10), .E11(unit_matirx_2_e11));
  matrix_multi matrix_multi_2 (
    .a00(s00), .a01(s01), .a10(s10), .a11(s11), .b00(matrix_mux_2_c00), .b01(matrix_mux_2_c01),
    .b10(matrix_mux_2_c10), .b11(matrix_mux_2_c11), .c00(matrix_multi_2_c00), .c01(matrix_multi_2_c01),
    .c10(matrix_multi_2_c10), .c11(matrix_multi_2_c11));
  matrix_mux matrix_mux_3 (
    .a00(unit_matirx_2_e00), .a01(unit_matirx_2_e01), .a10(unit_matirx_2_e10), .a11(unit_matirx_2_e11),
    .b00(matrix_multi_2_c00), .b01(matrix_multi_2_c01), .b10(matrix_multi_2_c10), .b11(matrix_multi_2_c11),
    .sel(\begin ), .c00(matrix_mux_3_c00), .c01(matrix_mux_3_c01), .c10(matrix_mux_3_c10),
    .c11(matrix_mux_3_c11));
  not not_1 (en, freeze);
  grf S_matrix (
    .a00_in(matrix_mux_3_c00), .a01_in(matrix_mux_3_c01), .a10_in(matrix_mux_3_c10),
    .a11_in(matrix_mux_3_c11), .en(en), .clk(clk), .re(re), .a00_out(s00), .a01_out(s01), .a10_out(s10),
    .a11_out(s11));
  Multiplexer #(.width(32), .disabled(0)) multiplexer_1 (
    .in0({32{1'b0}}), .in1(s01), .out(out_4), .sel(freeze));  // open: en
endmodule

module matrix_begin (
  output [31:0] A00,
  output [31:0] A01,
  output [31:0] A10,
  output [31:0] A11
);


  assign A00 = 32'h1;
  assign A01 = 32'h1;
  assign A10 = 32'h1;
  assign A11 = {32{1'b0}};
endmodule

module unit_matirx (
  output [31:0] E00,
  output [31:0] E01,
  output [31:0] E10,
  output [31:0] E11
);


  assign E00 = 32'h1;
  assign E01 = {32{1'b0}};
  assign E10 = {32{1'b0}};
  assign E11 = 32'h1;
endmodule

module matrix_mux (
  input  [31:0] a00,
  input  [31:0] a01,
  input  [31:0] a10,
  input  [31:0] a11,
  input  [31:0] b00,
  input  sel,
  input  [31:0] b01,
  input  [31:0] b10,
  input  [31:0] b11,
  output [31:0] c00,
  output [31:0] c01,
  output [31:0] c10,
  output [31:0] c11
);

  Multiplexer #(.width(32), .disabled(0)) multiplexer_1 (.in0(a00), .in1(b00), .out(c00), .sel(sel));  // open: en
  Multiplexer #(.width(32), .disabled(0)) multiplexer_2 (.in0(a01), .in1(b01), .out(c01), .sel(sel));  // open: en
  Multiplexer #(.width(32), .disabled(0)) multiplexer_3 (.in0(a10), .in1(b10), .out(c10), .sel(sel));  // open: en
  Multiplexer #(.width(32), .disabled(0)) multiplexer_4 (.in0(a11), .in1(b11), .out(c11), .sel(sel));  // open: en
endmodule

module matrix_multi (
  input  [31:0] a00,
  input  [31:0] a01,
  input  [31:0] a10,
  input  [31:0] a11,
  input  [31:0] b00,
  input  [31:0] b01,
  input  [31:0] b10,
  input  [31:0] b11,
  output [31:0] c00,
  output [31:0] c01,
  output [31:0] c10,
  output [31:0] c11
);

  wire [31:0] multiplier_1_out, multiplier_2_out, multiplier_3_out, multiplier_4_out, multiplier_5_out,
       multiplier_6_out, multiplier_7_out, multiplier_8_out;

  Multiplier #(.width(32)) multiplier_1 (.a(a00), .b(b00), .out(multiplier_1_out));  // open: cin, cout
  Multiplier #(.width(32)) multiplier_2 (.a(a01), .b(b10), .out(multiplier_2_out));  // open: cin, cout
  Multiplier #(.width(32)) multiplier_3 (.a(a00), .b(b01), .out(multiplier_3_out));  // open: cin, cout
  Multiplier #(.width(32)) multiplier_4 (.a(a01), .b(b11), .out(multiplier_4_out));  // open: cin, cout
  Multiplier #(.width(32)) multiplier_5 (.a(a10), .b(b00), .out(multiplier_5_out));  // open: cin, cout
  Multiplier #(.width(32)) multiplier_6 (.a(a11), .b(b10), .out(multiplier_6_out));  // open: cin, cout
  Multiplier #(.width(32)) multiplier_7 (.a(a10), .b(b01), .out(multiplier_7_out));  // open: cin, cout
  Multiplier #(.width(32)) multiplier_8 (.a(a11), .b(b11), .out(multiplier_8_out));  // open: cin, cout
  Adder #(.width(32)) adder_1 (.a(multiplier_1_out), .b(multiplier_2_out), .out(c00));  // open: cin, cout
  Adder #(.width(32)) adder_2 (.a(multiplier_3_out), .b(multiplier_4_out), .out(c01));  // open: cin, cout
  Adder #(.width(32)) adder_3 (.a(multiplier_5_out), .b(multiplier_6_out), .out(c10));  // open: cin, cout
  Adder #(.width(32)) adder_4 (.a(multiplier_7_out), .b(multiplier_8_out), .out(c11));  // open: cin, cout
endmodule

module grf (
  input  [31:0] a00_in,
  input  [31:0] a01_in,
  input  [31:0] a10_in,
  input  [31:0] a11_in,
  input  en,
  input  clk,
  input  re,
  output [31:0] a00_out,
  output [31:0] a01_out,
  output [31:0] a10_out,
  output [31:0] a11_out
);

  Register #(.width(32)) register_1 (.D(a00_in), .en(en), .Q(a00_out), .clk(clk), .clr(re));
  Register #(.width(32)) register_2 (.D(a10_in), .en(en), .Q(a10_out), .clk(clk), .clr(re));
  Register #(.width(32)) register_3 (.D(a01_in), .en(en), .Q(a01_out), .clk(clk), .clr(re));
  Register #(.width(32)) register_4 (.D(a11_in), .en(en), .Q(a11_out), .clk(clk), .clr(re));

  // Other names for the same wires on the sheet: a00[31:0] = a00_in; a01[31:0] = a01_in; a10[31:0] = a10_in;
  //   a11[31:0] = a11_in
endmodule
