// Logisim project gate.circ as structural Verilog: 1 circuit, main circuit main
module main (
  input  [5:0] in_1,
  input  in_2,
  input  x,
  input  in_4,
  input  y,
  input  in_6,
  input  in_7,
  input  in_8,
  input  in_9,
  output out_10,
  output out_11,
  output out_12,
  output out_13
);

  wire and_1_out, and_2_out, not_1_out, not_2_out;
  wire [2:0] xnor_1_out;

  not not_1 (not_1_out, x);
  not not_2 (not_2_out, y);
  // Probe on xnor_1_out
  assign xnor_1_out = ~(in_1[2:0] ^ in_1[5:3]);  // XNOR_Gate xnor_1, 3 bits wide
  and and_1 (and_1_out, not_1_out, y);
  and and_2 (and_2_out, x, not_2_out);
  xnor xnor_2 (out_12, in_6, in_7);
  nor nor_1 (out_13, in_8, in_9);
  or or_1 (out_11, and_1_out, and_2_out);
  Decoder decoder_1 ();  // open: out0, out1, sel, en
  // Probe on in_2

  assign in_4 = in_2;
  assign out_10 = in_2;

  // Other names for the same wires on the sheet: _1 = in_2

  // Notes on the sheet:
  //   xor gate
  //   xnor gate
  //   NOR gate
  //   probe
  //   Tunnel wiring
endmodule
