// Logisim project swap_circuit_byfzc.circ as structural Verilog
module swap (
  input  I1,
  input  I2,
  input  S,
  output out_4,
  output out_5
);

  wire and_1_out, and_2_out, and_3_out, and_4_out, not_1_out, not_2_out;

  not not_1 (not_1_out, S);
  not not_2 (not_2_out, S);
  and and_1 (and_1_out, I2, S);
  or or_1 (out_4, and_1_out, and_2_out);
  and and_2 (and_2_out, I1, not_1_out);
  and and_3 (and_3_out, I2, not_2_out);
  or or_2 (out_5, and_3_out, and_4_out);
  and and_4 (and_4_out, I1, S);
endmodule
