// Logisim project 八选一选择器完成函数.circ as structural Verilog: 1 circuit, main circuit main
module main (
  input  D,
  input  E,
  input  C,
  input  B,
  input  A,
  output F
);

  wire D_nE_out, nD_nE_out, nDE_out, not_1_out, not_2_out, or_1_out, or_2_out, or_3_out, or_4_out, or_5_out,
       or_6_out, or_7_out, or_8_out;

  not not_1 (not_1_out, D);
  not not_2 (not_2_out, E);
  and nD_nE (nD_nE_out, not_1_out, not_2_out);
  // AND_Gate DE has open pins: in0=D, in1=E, out=open
  buf D_nE (D_nE_out, D);  // AND_Gate
  and nDE (nDE_out, not_1_out, E);
  or or_1 (or_1_out, nD_nE_out, D_nE_out);
  or or_2 (or_2_out, D_nE_out, nDE_out);
  or or_3 (or_3_out, nDE_out, D_nE_out);
  or or_4 (or_4_out, nD_nE_out, D_nE_out);
  or or_5 (or_5_out, nDE_out, D_nE_out);
  or or_6 (or_6_out, nD_nE_out, D_nE_out);
  or or_7 (or_7_out, nDE_out, D_nE_out);
  or or_8 (or_8_out, nD_nE_out, D_nE_out);
  Multiplexer #(.select(3)) multiplexer_1 (
    .in0(or_2_out), .in1(or_1_out), .in2(or_3_out), .in3(or_4_out), .in4(or_5_out), .in5(or_6_out),
    .in6(or_7_out), .in7(or_8_out), .out(F), .sel({C, B, A}));  // open: en
endmodule
