// Logisim project 排序电路.circ as structural Verilog
module main (
  input  I1,
  input  I2,
  input  S,
  output out_4,
  output out_5
);

  wire and_1_out, and_2_out, and_3_out, and_4_out, not_1_out, not_2_out;

  and and_1 (and_1_out, I2, S);
  and and_2 (and_2_out, I1, not_1_out);
  not not_1 (not_1_out, S);
  and and_3 (and_3_out, I2, not_2_out);
  not not_2 (not_2_out, S);
  and and_4 (and_4_out, I1, S);
  or or_1 (out_4, and_1_out, and_2_out);
  or or_2 (out_5, and_3_out, and_4_out);
endmodule

module _1bit_swap (
  input  I1,
  input  I2,
  input  S,
  output out_4,
  output out_5
);

  wire and_1_out, and_2_out, and_3_out, and_4_out, not_1_out, not_2_out;

  and and_1 (and_1_out, I2, S);
  and and_2 (and_2_out, I1, not_1_out);
  not not_1 (not_1_out, S);
  and and_3 (and_3_out, I2, not_2_out);
  not not_2 (not_2_out, S);
  and and_4 (and_4_out, I1, S);
  or or_1 (out_4, and_1_out, and_2_out);
  or or_2 (out_5, and_3_out, and_4_out);
endmodule

module _4bit_swap (
  input  [3:0] in_1,
  input  [3:0] in_2,
  input  in_3,
  output [3:0] out_4,
  output [3:0] out_5
);

  _1bit_swap u_1bit_swap_1 (.I1(in_1[0]), .I2(in_2[0]), .S(in_3), .out_4(out_4[0]), .out_5(out_5[0]));
  _1bit_swap u_1bit_swap_2 (.I1(in_1[1]), .I2(in_2[1]), .S(in_3), .out_4(out_4[1]), .out_5(out_5[1]));
  _1bit_swap u_1bit_swap_3 (.I1(in_1[2]), .I2(in_2[2]), .S(in_3), .out_4(out_4[2]), .out_5(out_5[2]));
  _1bit_swap u_1bit_swap_4 (.I1(in_1[3]), .I2(in_2[3]), .S(in_3), .out_4(out_4[3]), .out_5(out_5[3]));
endmodule
