// Logisim project 斐波那契.circ as structural Verilog: 2 circuits, main circuit main
module main (
  input  [2:0] in_1,
  output [3:0] out_2
);

  wire clock_1_out, comparator_1_eq, comparator_2_eq, comparator_2_lt, or_1_out;
  wire [2:0] counter_1_q;
  wire [3:0] adder_1_out, multiplexer_1_out, register_2_q;

  Counter #(.width(3), .max('h7)) counter_1 (.Q(counter_1_q), .clk(or_1_out));  // open: load, D, count, carry, clr
  Multiplexer #(.width(4)) multiplexer_1 (
    .in0(adder_1_out), .in1(4'b0001), .out(multiplexer_1_out), .sel(comparator_1_eq));  // open: en
  Comparator #(.width(3), .mode("unsigned")) comparator_1 (
    .a(3'b000), .b(counter_1_q), .eq(comparator_1_eq));  // open: gt, lt
  Comparator #(.width(3), .mode("unsigned")) comparator_2 (
    .a(in_1), .b(counter_1_q), .eq(comparator_2_eq), .lt(comparator_2_lt));  // open: gt
  Clock clock_1 (.out(clock_1_out));
  Register #(.width(4)) register_1 (.D(multiplexer_1_out), .Q(out_2), .clk(or_1_out));  // open: en, clr
  or or_1 (or_1_out, comparator_2_eq, comparator_2_lt, clock_1_out);
  Register #(.width(4)) register_2 (.D(out_2), .Q(register_2_q), .clk(or_1_out));  // open: en, clr
  Adder #(.width(4)) adder_1 (.a(out_2), .b(register_2_q), .out(adder_1_out));  // open: cin, cout
endmodule

module test (
  input  [2:0] in_1,
  output [3:0] out_2
);

  wire clock_1_out, counter_1_carry;
  wire [3:0] main_1_out_2;

  Counter #(.width(6), .max('h3f)) counter_1 (
    .carry(counter_1_carry), .clk(clock_1_out));  // open: load, D, count, Q, clr
  Clock clock_1 (.out(clock_1_out));
  main main_1 (.in_1(in_1), .out_2(main_1_out_2));
  Register #(.width(4)) register_1 (.D(main_1_out_2), .Q(out_2), .clk(counter_1_carry));  // open: en, clr
endmodule
