// Logisim project 组合电路.circ as structural Verilog: 9 circuits, main circuit main
module main (
  input  [1:0] in_1,
  input  [1:0] in_2,
  input  [1:0] in_3,
  input  [1:0] in_4,
  input  [1:0] in_5,
  output [1:0] out_6,
  output [1:0] out_7,
  output [1:0] out_8,
  output [1:0] out_9,
  output [1:0] out_10
);

  wire decoder_1_out0, decoder_1_out1, decoder_1_out2, decoder_1_out3;

  Multiplexer #(.select(2), .width(2)) multiplexer_1 (
    .in1(in_2), .in3(in_2), .out(out_10), .sel(in_4));  // open: in0, in2, en
  Priority_Encoder priority_encoder_1 ();  // open: in0, in1, in2, in3, in4, in5, in6, in7, out, en_in, gs, en_out
  BitSelector bitselector_1 ();  // open: in, out, sel
  Demultiplexer #(.select(2), .width(2)) demultiplexer_1 (
    .out0(out_6), .out1(out_7), .out2(out_8), .out3(out_9), .in(in_1), .sel(in_3));  // open: en
  Decoder #(.select(2)) decoder_1 (
    .out0(decoder_1_out0), .out1(decoder_1_out1), .out2(decoder_1_out2), .out3(decoder_1_out3), .sel(in_5));  // open: en
endmodule

module _2_1_mux (
  input  in_1,
  input  in_2,
  input  in_3,
  output out_4
);

  wire and_1_out, and_2_out, not_1_out;

  not not_1 (not_1_out, in_3);
  and and_1 (and_1_out, in_1, not_1_out);
  and and_2 (and_2_out, in_2, in_3);
  or or_1 (out_4, and_1_out, and_2_out);
endmodule

module _4_1_mux (
  input  in_1,
  input  in_2,
  input  in_3,
  input  in_4,
  input  in_5,
  input  in_6,
  output out_7
);

  wire n2_1_mux_1_out_4, n2_1_mux_2_out_4;

  _2_1_mux u_2_1_mux_1 (.in_1(in_1), .in_2(in_2), .in_3(in_5), .out_4(n2_1_mux_1_out_4));
  _2_1_mux u_2_1_mux_2 (.in_1(in_3), .in_2(in_4), .in_3(in_5), .out_4(n2_1_mux_2_out_4));
  _2_1_mux u_2_1_mux_3 (.in_1(n2_1_mux_1_out_4), .in_2(n2_1_mux_2_out_4), .in_3(in_6), .out_4(out_7));
endmodule

module or_gate (
  input  x,
  input  y,
  output z,
  output d
);

  wire not_1_out;

  or or_1 (z, x, y);
  not not_1 (not_1_out, y);
  and and_1 (d, x, not_1_out);
endmodule

module exercise (
  input  a,
  input  b,
  input  c,
  output y
);

  wire and_1_out, and_2_out, not_1_out;

  not not_1 (not_1_out, c);
  and and_1 (and_1_out, b, c);
  and and_2 (and_2_out, a, not_1_out);
  or or_1 (y, and_1_out, and_2_out);
endmodule

module e1 (
  input  a,
  input  b,
  input  c,
  output y
);

  wire and_1_out, and_2_out, not_1_out;

  not not_1 (not_1_out, c);
  and and_1 (and_1_out, b, c);
  and and_2 (and_2_out, a, not_1_out);
  or or_1 (y, and_1_out, and_2_out);
endmodule

module e2 (
  input  a,
  input  b,
  input  c,
  output y
);

  wire nand_1_out, nand_2_out, nand_3_out;

  nand nand_1 (nand_1_out, c, c);
  nand nand_2 (nand_2_out, b, c);
  nand nand_3 (nand_3_out, a, nand_1_out);
  nand nand_4 (y, nand_2_out, nand_3_out);
endmodule

module e3 (
  input  a,
  input  b,
  input  c,
  output y
);

  wire and_1_out, and_2_out, not_1_out;

  not not_1 (not_1_out, c);
  and and_1 (and_1_out, b, c);
  and and_2 (and_2_out, a, not_1_out);
  or or_1 (y, and_1_out, and_2_out);
endmodule

module e4 (
  input  a,
  input  b,
  input  c,
  output y
);

  wire not_1_out, or_1_out, or_2_out;

  not not_1 (not_1_out, c);
  or or_1 (or_1_out, a, c);
  or or_2 (or_2_out, b, not_1_out);
  and and_1 (y, or_1_out, or_2_out);
endmodule
